// Logisim project 8.2.circ as structural Verilog: 1 circuit, main circuit main
module main (
);

  wire and_1_out, and_2_out, and_3_out, and_4_out, not_1_out, not_2_out, not_3_out, or_1_out, undriven,
       undriven_2, undriven_3;

  not not_1 (not_1_out, undriven_2);
  not not_2 (not_2_out, undriven_3);
  not not_3 (not_3_out, undriven);
  and and_1 (and_1_out, not_1_out, not_2_out, not_3_out);
  and and_2 (and_2_out, not_1_out, undriven_3, undriven);
  and and_3 (and_3_out, undriven_2, undriven_3, not_3_out);
  and and_4 (and_4_out, undriven_2, undriven_3, undriven);
  or or_1 (or_1_out, and_1_out, and_2_out, and_3_out, and_4_out);
  LED led_1 (.in(or_1_out));

  // Notes on the sheet:
  //   A
  //   B
  //   C
  //   B
  //   A
  //   C
  //   ¬C
  //   ¬A
  //   ¬B
endmodule
